// Logisim project circuit.circ as structural Verilog: 3 circuits, main circuit main
module main (
  input  D,
  input  RES,
  output FF0,
  output FF1,
  output FF2,
  output out_6,
  output out_7,
  output out_8
);

  wire CLK_out;

  Clock CLK (.out(CLK_out));
  MasterSlave_D_Trigger masterslave_d_trigger_1 (.D(D), .CLK(CLK_out), .RES(RES), .Q(FF0));  // open: N_Q
  TTL_D_Trigger ttl_d_trigger_1 (.D(D), .CLK(CLK_out), .RES(RES), .Q(out_6));  // open: N_Q
  MasterSlave_D_Trigger masterslave_d_trigger_2 (.D(FF0), .CLK(CLK_out), .RES(RES), .Q(FF1));  // open: N_Q
  TTL_D_Trigger ttl_d_trigger_2 (.D(out_6), .CLK(CLK_out), .RES(RES), .Q(out_7));  // open: N_Q
  MasterSlave_D_Trigger masterslave_d_trigger_3 (.D(FF1), .CLK(CLK_out), .RES(RES), .Q(FF2));  // open: N_Q
  TTL_D_Trigger ttl_d_trigger_3 (.D(out_7), .CLK(CLK_out), .RES(RES), .Q(out_8));  // open: N_Q
endmodule

module MasterSlave_D_Trigger (
  input  D,
  input  CLK,
  input  RES,
  output Q,
  output N_Q
);

  wire nand_1_out, nand_2_out, nand_3_out, nand_4_out, not_1_out;

  not not_1 (not_1_out, RES);
  nand nand_1 (nand_1_out, nand_4_out, nand_2_out);
  nand nand_2 (nand_2_out, nand_1_out, CLK, not_1_out);
  nand nand_3 (nand_3_out, nand_2_out, CLK, nand_4_out);
  nand nand_4 (nand_4_out, nand_3_out, D, not_1_out);
  nand nand_5 (Q, nand_2_out, N_Q);
  nand nand_6 (N_Q, Q, nand_3_out, not_1_out);

  // Notes on the sheet:
  //   S
  //   R
endmodule

module TTL_D_Trigger (
  input  D,
  input  CLK,
  input  RES,
  output Q,
  output N_Q
);

  wire n7400_1_pin1, n7400_1_pin2, n7400_1_pin3, n7404_1_pin2, n7410_1_pin6;

  _7404 u_7404_1 (
    .pin1(RES), .pin2(n7404_1_pin2));  // open: pin3, pin4, pin5, pin6, pin13, pin12, pin11, pin10, pin9, pin8
  _7400 u_7400_1 (
    .pin1(n7400_1_pin1), .pin2(n7400_1_pin2), .pin3(n7400_1_pin3), .pin4(n7400_1_pin2), .pin5(N_Q), .pin6(Q));  // open: pin13, pin12, pin11, pin10, pin9, pin8
  _7410 u_7410_1 (
    .pin1(n7400_1_pin3), .pin2(CLK), .pin3(n7400_1_pin2), .pin4(CLK), .pin5(n7400_1_pin1),
    .pin6(n7410_1_pin6), .pin13(n7404_1_pin2), .pin12(n7400_1_pin2), .pin11(n7410_1_pin6), .pin10(D),
    .pin9(n7404_1_pin2), .pin8(n7400_1_pin1));
  _7410 u_7410_2 (
    .pin1(Q), .pin2(n7410_1_pin6), .pin13(n7404_1_pin2), .pin12(N_Q));  // open: pin3, pin4, pin5, pin6, pin11, pin10, pin9, pin8

  // Notes on the sheet:
  //   s
  //   r
endmodule
