// Logisim project circuit.circ as structural Verilog: 4 circuits, main circuit main
module main (
  input  D0,
  input  D1,
  input  DL,
  input  DR,
  input  S0,
  input  S1,
  input  CLK,
  output Q1,
  output Q0
);

  wire multiplexer_1_out, multiplexer_2_out, not_1_out, not_2_out;

  Multiplexer #(.select(2)) multiplexer_1 (
    .in0(Q1), .in1(DR), .in2(Q0), .in3(D1), .out(multiplexer_1_out), .sel({S1, S0}));
  J_K_Flip_Flop j_k_ff_1 (.J(multiplexer_1_out), .K(not_1_out), .clk(CLK), .Q(Q1));  // open: Qn, preset, reset
  not not_1 (not_1_out, multiplexer_1_out);
  Multiplexer #(.select(2)) multiplexer_2 (
    .in0(Q0), .in1(Q1), .in2(DL), .in3(D0), .out(multiplexer_2_out), .sel({S1, S0}));
  J_K_Flip_Flop j_k_ff_2 (.J(multiplexer_2_out), .K(not_2_out), .clk(CLK), .Q(Q0));  // open: Qn, preset, reset
  not not_2 (not_2_out, multiplexer_2_out);
  _74153 #(.ShowInternalStructure("true")) u_74153_1 ();  // open: pin1, pin2, pin3, pin4, pin5, pin6, pin7, pin15, pin14, pin13, pin12, pin11, pin10, pin9

  // Notes on the sheet:
  //   Q1
  //   Q0
endmodule

module parzival (
  input  D,
  input  Res,
  output Q1,
  output Q0
);

  wire clock_1_out;

  D_Flip_Flop d_ff_1 (.D(D), .clk(clock_1_out), .Q(Q1), .reset(Res));  // open: Qn, preset
  Clock clock_1 (.out(clock_1_out));
  D_Flip_Flop d_ff_2 (.D(Q1), .clk(clock_1_out), .Q(Q0), .reset(Res));  // open: Qn, preset
endmodule

module TTL74151 (
  input  S0,
  input  S1,
  input  D1,
  input  D0,
  input  DL,
  input  DR,
  input  CLK,
  input  S,
  input  R,
  output Q1,
  output Q0
);

  wire n74151_1_pin5, n74151_1_pin6, n74151_1_pin15, n74151_2_pin5, n74151_2_pin6;

  J_K_Flip_Flop j_k_ff_1 (.J(n74151_1_pin5), .K(n74151_1_pin6), .clk(CLK), .Q(Q1), .preset(S), .reset(R));  // open: Qn
  _74151 #(.ShowInternalStructure("true")) u_74151_1 (
    .pin1(D1), .pin2(Q0), .pin3(DR), .pin4(Q1), .pin5(n74151_1_pin5), .pin6(n74151_1_pin6),
    .pin15(n74151_1_pin15), .pin14(n74151_1_pin15), .pin13(n74151_1_pin15), .pin12(n74151_1_pin15),
    .pin11(S0), .pin10(S1), .pin9(n74151_1_pin15));  // open: pin7
  _74151 #(.ShowInternalStructure("true")) u_74151_2 (
    .pin1(D0), .pin2(DL), .pin3(Q1), .pin4(Q0), .pin5(n74151_2_pin5), .pin6(n74151_2_pin6),
    .pin15(n74151_1_pin15), .pin14(n74151_1_pin15), .pin13(n74151_1_pin15), .pin12(n74151_1_pin15),
    .pin11(S0), .pin10(S1), .pin9(n74151_1_pin15));  // open: pin7
  J_K_Flip_Flop j_k_ff_2 (.J(n74151_2_pin5), .K(n74151_2_pin6), .clk(CLK), .Q(Q0), .preset(S), .reset(R));  // open: Qn
  // also tied to GND on the sheet: n74151_1_pin15
endmodule

module TTL74153 (
  input  D0,
  input  D1,
  input  DL,
  input  DR,
  input  S0,
  input  S1,
  input  CLK,
  output Q1,
  output Q0
);

  wire n74153_1_pin1, n74153_1_pin7, n74153_1_pin9, not_1_out, not_2_out;

  J_K_Flip_Flop j_k_ff_1 (.J(n74153_1_pin7), .K(not_1_out), .clk(CLK), .Q(Q1));  // open: Qn, preset, reset
  not not_1 (not_1_out, n74153_1_pin7);
  _74153 #(.ShowInternalStructure("true")) u_74153_1 (
    .pin1(n74153_1_pin1), .pin2(S1), .pin3(D1), .pin4(Q0), .pin5(DR), .pin6(Q1), .pin7(n74153_1_pin7),
    .pin15(n74153_1_pin1), .pin14(S0), .pin13(D0), .pin12(DL), .pin11(Q1), .pin10(Q0), .pin9(n74153_1_pin9));
  J_K_Flip_Flop j_k_ff_2 (.J(n74153_1_pin9), .K(not_2_out), .clk(CLK), .Q(Q0));  // open: Qn, preset, reset
  not not_2 (not_2_out, n74153_1_pin9);
  // also tied to GND on the sheet: n74153_1_pin1

  // Notes on the sheet:
  //   Q1
  //   Q0
endmodule
